# Fritzing sketch calibration-circuit (saved by Fritzing 1.0.6)
breadboards: 1

parts:
  R = Resistor [tolerance=±5% resistance=110 package="1206 [SMD]"]
  Arduino_UNO = Arduino Uno (Rev3)
  RL = Resistor [tolerance=±5% resistance=220 package="1206 [SMD]"]
  L1 = Inductor [package="400 mil [THT]"]
  S = Pushbutton [package="[THT]"]
  LED1 = LED - 5mm [color="Green (555nm)" current=0.030A package="5 mm [THT]"]

nets:
  N1: R.Pin_0, Arduino_UNO.A0, L1.pin_0
  N2: R.Pin_1, Arduino_UNO.GND, S.Pin_3, S.Pin_4, LED1.cathode
  N3: Arduino_UNO.D5_PWM, L1.pin_1
  N4: Arduino_UNO.D6_PWM, RL.Pin_1
  N5: Arduino_UNO.D7, S.Pin_1, S.Pin_2
  N6: RL.Pin_0, LED1.anode
