# Fritzing sketch circuit (saved by Fritzing 1.0.6)
breadboards: 1

parts:
  Arduino = Arduino Uno (Rev3)
  ADS1115 = ADS1115
  P1 = S1133 Si Photodiode [package="8mm Ceramic [THT]"]
  OLED = Grove OLED 128x96
  AD8628 = IC, DIP package, 8 pins [chip_label=AD8628]
  R1 = Resistor [tolerance=±5% resistance=10M package="2010 [SMD]"]
  C1 = Tantalum Capacitor [capacitance=10pF voltage=35V package="C 6032 [SMD, tantalum]"]
  VCC1 = Battery block 9V [internal_resistance=0.1Ω]

nets:
  N1: Arduino.A4/SDA, ADS1115.SDA, OLED.SCL
  N2: Arduino.A5/SCL, ADS1115.SCL, OLED.SDA
  5V: Arduino.5V, ADS1115.VDD, OLED.VCC
  GND: Arduino.GND, ADS1115.GND, ADS1115.ADDR, OLED.GND, AD8628.pin3, AD8628.pin4, VCC1.-
  N3: ADS1115.A0, P1.anode, AD8628.pin6, R1.Pin_1, C1.-
  N4: P1.cathode, AD8628.pin2, R1.Pin_0, C1.+
  N5: AD8628.pin7, VCC1.+

custom parts:
  ADS1115: ADC ADS1115
