# Fritzing sketch data-converter-circuit (saved by Fritzing 1.0.6)
breadboards: 1

parts:
  PSD = S1133 Si Photodiode [package="8mm Ceramic [THT]"]
  Arduino_UNO = Arduino Ethernet Shield (Rev3)
  ADS1115 = ADS1115
  R1 = Resistor [tolerance=±2% resistance=100000 package="2010 [SMD]"]
  Laser = LEDs [package=led10mm]
  VCC1 = Battery block 9V [internal_resistance=0.1Ω]
  AD8628 = DIP - 8 pins [chip_label=AD8628 package="DIP (Dual Inline) [THT]"]
  LED = smd LED [color="Yellow (592nm)" package="0603 [SMD]"]
  RL = Resistor [tolerance=±2% power=0.25W resistance=100000 package=THT]
  AD8628_2 = DIP - 8 pins [chip_label=AD8628 package="DIP (Dual Inline) [THT]"]
  R2 = Resistor [tolerance=±2% resistance=100000 package="2010 [SMD]"]

nets:
  N1: PSD.cathode, AD8628_2.+IN
  N2: PSD.anode, AD8628.+IN
  N3: Arduino_UNO.A4/SDA, ADS1115.SDA
  N4: Arduino_UNO.A5/SCL, ADS1115.SCL
  N5: Arduino_UNO.PWM_D6, RL.Pin_0
  5V: Arduino_UNO.5V, ADS1115.VDD, AD8628.V+, AD8628_2.V+
  GND: Arduino_UNO.GND, ADS1115.GND, ADS1115.ADDR, AD8628.V-, LED.cathode, AD8628_2.V-
  N6: ADS1115.A0, R1.Pin_1, AD8628.OUT
  N7: ADS1115.A1, AD8628_2.OUT, R2.Pin_1
  N8: R1.Pin_0, AD8628.-IN
  N9: Laser.C, VCC1.-
  N10: Laser.A, VCC1.+
  N11: LED.anode, RL.Pin_1
  N12: AD8628_2.-IN, R2.Pin_0

custom parts:
  ADS1115: ADC ADS1115
  DIP - 8 pins: A DIP stand-in part for whatever IC you want. With 8 pins on a 300mil dual inline package (DIP) footprint.
