# Fritzing sketch generator-circuit (saved by Fritzing 1.0.6)

parts:
  Si4713 = Si4713 Stereo FM Transmitter
  ANT = Antenna
  Arduino_UNO = Arduino Uno (Rev3)
  AM = Audio Jack (TRS) 3.5mm [package="4Ucon 08780 [THT]"]

nets:
  N1: Si4713.ANT, ANT.antenna_lead
  N2: Si4713.RIN, AM.Ring
  N3: Si4713.LIN, AM.Tip
  VIN: Si4713.VIN, Arduino_UNO.5V
  GND: Si4713.GND, Arduino_UNO.GND, AM.Sleeve
  N4: Si4713.SDA, Arduino_UNO.A4/SDA
  N5: Si4713.SCL, Arduino_UNO.A5/SCL
  N6: Si4713.RST, Arduino_UNO.D12/MISO

custom parts:
  Si4713 Stereo FM Transmitter: Yaaar! Become your very own pirate radio station with this FM radio transmitter. This breakout board, based on the best-of-class Si4713, is an all-in-one stereo audio FM transmitter that can also transmit RDS/RBDS data!
